# Fritzing sketch Cable Notation (saved by Fritzing 0.9.4)
breadboards: 1

parts:
  Parça1 = Arduino Uno (Rev3) - ICSP
  LED1 = 7-SEGMENT-4DIGIT [package=7-segment-4digit]
  R1 = Resistor [tolerance=±5% resistance=220 package=THT]
  R2 = Resistor [tolerance=±5% resistance=220 package=THT]
  R3 = Resistor [tolerance=±5% resistance=220 package=THT]
  R4 = Resistor [tolerance=±5% resistance=220 package=THT]
  LED2 = LED - 5mm [color="Red (633nm)" package="5 mm [THT]"]
  R5 = Resistor [tolerance=±5% resistance=220 package=THT]
  LED3 = LED - 5mm [color="Green (570nm)" package="5 mm [THT]"]
  R6 = Resistor [tolerance=±5% resistance=220 package=THT]
  S1 = Momentary Switch [package=ksa_sealed_tac_switch]
  R7 = Resistor [tolerance=±5% resistance=220 package=THT]
  J1 = Piezo Speaker
  R8 = Resistor [tolerance=±5% resistance=220 package=THT]

nets:
  N1: Parça1.A0, S1.2, R7.Pin_1
  N2: Parça1.A1, R6.Pin_0
  N3: Parça1.A2, R5.Pin_0
  N4: Parça1.A3, R8.Pin_0
  N5: Parça1.D8, R2.Pin_1
  N6: Parça1.D9_PWM, R3.Pin_1
  N7: Parça1.D10_PWM/SS, LED1.14
  N8: Parça1.D11_PWM/MOSI, LED1.15
  N9: Parça1.D12/MISO, R4.Pin_0
  N10: Parça1.D13/SCK, LED1.1
  N11: Parça1.D3_PWM, LED1.2
  N12: Parça1.D4, LED1.4
  N13: Parça1.D5_PWM, LED1.5
  N14: Parça1.D6_PWM, R1.Pin_1
  N15: Parça1.D7, LED1.11
  N16: Parça1.5V, S1.4
  N17: Parça1.GND, LED2.cathode, LED3.cathode, R7.Pin_0, J1.pin2
  N18: LED1.6, R1.Pin_0
  N19: LED1.13, R3.Pin_0
  N20: LED1.16, R4.Pin_1
  N21: LED2.anode, R5.Pin_1
  N22: LED3.anode, R6.Pin_1
  N23: J1.pin1, R8.Pin_1

notes:
  1 2 3 4 5 6
  12 11 10 9 8 7
