# Fritzing sketch Cable Notation (saved by Fritzing 0.9.4)
breadboards: 2

parts:
  Disp1 = LBT2088AH [part_number=LBT2088AH]
  Parça1 = Arduino Uno (Rev3) - ICSP
  R1 = Resistor [tolerance=±5% resistance=220 package=THT]
  R2 = Resistor [tolerance=±5% resistance=220 package=THT]
  R3 = Resistor [tolerance=±5% resistance=220 package=THT]
  R4 = Resistor [tolerance=±5% resistance=220 package=THT]
  R5 = Resistor [tolerance=±5% resistance=220 package=THT]
  R6 = Resistor [tolerance=±5% resistance=220 package=THT]
  R7 = Resistor [tolerance=±5% resistance=220 package=THT]
  R8 = Resistor [tolerance=±5% resistance=220 package=THT]
  Parça2 = Thumb Joystick
  J1 = Piezo Speaker
  R9 = Resistor [tolerance=±5% resistance=220 package=THT]

nets:
  N1: Disp1.pin1, R1.Pin_0
  N2: Disp1.pin2, R2.Pin_0
  N3: Disp1.pin_3, Parça1.D7
  N4: Disp1.pin_4, Parça1.D6_PWM
  N5: Disp1.pin_5, R6.Pin_0
  N6: Disp1.pin_6, Parça1.D4
  N7: Disp1.pin_7, R7.Pin_0
  N8: Disp1.pin_8, R8.Pin_0
  N9: Parça1.A0, R8.Pin_1
  N10: Parça1.A1, R3.Pin_0
  N11: Parça1.A2, R5.Pin_1
  N12: Parça1.A3, R9.Pin_0
  N13: Parça1.A4/SDA, Parça2.VERT
  N14: Parça1.A5/SCL, Parça2.HORZ
  N15: Parça1.D9_PWM, R6.Pin_1
  N16: Parça1.D10_PWM/SS, R2.Pin_1
  N17: Parça1.D11_PWM/MOSI, R7.Pin_1
  N18: Parça1.D12/MISO, R1.Pin_1
  N19: Parça1.D13/SCK, R4.Pin_1
  N20: Parça1.5V, Parça2.SEL
  GND: Parça1.GND, Parça2.GND, J1.pin2
  N21: J1.pin1, R9.Pin_1

notes:
  sw vry vrx +5v gnd
  + -
